# Fritzing sketch WemosD1Mini (saved by Fritzing 0.9.3b)

parts:
  WeMos_D1_Mini1 = WeMos D1 Mini
  Driver1 = 28BYJ-48 Driver Module [part_number=ULN2003 package=THT]
  Driver2 = 28BYJ-48 Driver Module [part_number=ULN2003 package=THT]
  SM1 = 28BYJ-48 Stepper Motor [part_number=28BYJ-48]
  SM2 = 28BYJ-48 Stepper Motor [part_number=28BYJ-48]
  Power_plug_5V = Power plug
  S1 = SPST Switch [package=switche-dpdt]
  R1 = Resistor [tolerance=±5% resistance=100k package=THT]
  R2 = Resistor [tolerance=±5% resistance=100k package=THT]
  S4 = Round Pushbutton

nets:
  N1: WeMos_D1_Mini1.5V, Driver1.Vmotor, Driver2.Vmotor, S1.P, S4.leg0
  N2: WeMos_D1_Mini1.D0, S1.O, R2.Pin_0
  N3: WeMos_D1_Mini1.D1, Driver1.IN2
  N4: WeMos_D1_Mini1.D2, Driver1.IN3
  N5: WeMos_D1_Mini1.D3, Driver1.IN4
  N6: WeMos_D1_Mini1.D5, Driver2.IN1
  N7: WeMos_D1_Mini1.D6, Driver2.IN2
  N8: WeMos_D1_Mini1.D7, Driver2.IN3
  N9: WeMos_D1_Mini1.D8, Driver2.IN4
  GND: WeMos_D1_Mini1.G, Driver1.GND, Driver2.GND, Power_plug_5V.GND, R1.Pin_1, R2.Pin_1
  N10: WeMos_D1_Mini1.RX, Driver1.IN1
  N11: WeMos_D1_Mini1.TX, S1.S, R1.Pin_0
  N12: Driver1.blue-pin, SM1.blue-pin
  N13: Driver1.pink-pin, SM1.pink-pin
  N14: Driver1.yellow-pin, SM1.yellow-pin
  N15: Driver1.orange-pin, SM1.orange-pin
  N16: Driver1.red-pin, SM1.red-pin
  N17: Driver2.blue-pin, SM2.blue-pin
  N18: Driver2.pink-pin, SM2.pink-pin
  N19: Driver2.yellow-pin, SM2.yellow-pin
  N20: Driver2.orange-pin, SM2.orange-pin
  N21: Driver2.red-pin, SM2.red-pin
  N22: Power_plug_5V.VCC, S4.leg1

custom parts:
  28BYJ-48 Driver Module: ULN2003 Driver Module for the 28BYJ-48 Unipolar Stepper Motor LED A - Blue wire - Bottom coil left LED B - Pink wire - Top coil left LED C - Yellow wire - Bottom coil right LED D - Orange wire - Top coil right Common rail - red Connector pins: blue - pink - yellow - orange - red Control pins - IN1 to IN4 Power pins - GND & Vmotor (5-12V) On/Off jumper (if removed, power to motor is cut).
  28BYJ-48 Stepper Motor: Unipolar Stepper Motor 28BYJ-48 Top coil - pink & orange Bottom coil - blue & yellow Common rail - red Connector pins: blue - pink - yellow - orange - red
